// Logisim project Microprocessor.circ as structural Verilog: 4 circuits, main circuit CPU
module CPU (
  input  Reset
);

  wire and_1_out, and_2_out, and_3_out, CLK_out, multiplexer_3_out, nor_1_out, not_1_out, not_2_out,
       or_1_out, setRegister_nf, setRegister_setregister, setRegister_zf, ucontrol_1_immpresent,
       ucontrol_1_jump, ucontrol_1_l___0___s___1, ucontrol_1_mem___1_alu___0, ucontrol_1_poweron,
       ucontrol_1_setflag, ucontrol_1_wb;
  wire [1:0] ucontrol_1_seljump;
  wire [15:0] adder_1_out, bit_extender_1_out, bregs_1_reg1out, bregs_1_reg2out, bregs_1_regaout,
       bregs_1_regbout, bregs_1_regcout, bregs_1_regdout, multiplexer_1_out, multiplexer_2_out,
       multiplexer_4_out, multiplexer_5_out, PC_q, ram_1_data, ram_2_data, setRegister_outputalu;

  Clock CLK (.out(CLK_out));
  Register #(.width(16)) PC (.D(multiplexer_1_out), .en(ucontrol_1_poweron), .Q(PC_q), .clk(CLK_out), .clr(Reset));
  Adder #(.width(16)) adder_1 (.a(PC_q), .b(16'h1), .out(adder_1_out));  // open: cin, cout
  RAM #(.addrWidth(16), .dataWidth(16), .bus("separate")) ram_1 (
    .addr(PC_q), .data(ram_1_data), .ld(1'b1));  // open: din, str, sel, clk, clr
  Multiplexer #(.width(16), .enable("false")) multiplexer_1 (
    .in0(adder_1_out), .in1(multiplexer_4_out), .out(multiplexer_1_out), .sel(and_1_out));
  UControl ucontrol_1 (
    .setFlag(ucontrol_1_setflag), .WB(ucontrol_1_wb), .Mem___1_ALU___0(ucontrol_1_mem___1_alu___0),
    .L___0___S___1(ucontrol_1_l___0___s___1), .Instruction(ram_1_data), .Jump(ucontrol_1_jump),
    .PowerOn(ucontrol_1_poweron), .immPresent(ucontrol_1_immpresent), .selJump(ucontrol_1_seljump));
  // Probe on bregs_1_regdout
  // Probe on bregs_1_regcout
  // Probe on bregs_1_regbout
  // Probe on bregs_1_regaout
  assign bit_extender_1_out = {{8{ram_1_data[7]}}, ram_1_data[7:0]};  // Bit_Extender bit_extender_1
  and and_1 (and_1_out, multiplexer_3_out, ucontrol_1_jump);
  Multiplexer #(.width(16), .enable("false")) multiplexer_2 (
    .in0(setRegister_outputalu), .in1(ram_2_data), .out(multiplexer_2_out), .sel(ucontrol_1_mem___1_alu___0));
  and and_2 (and_2_out, or_1_out, ~CLK_out);  // AND_Gate
  Multiplexer #(.select(2), .enable("false")) multiplexer_3 (
    .in0(setRegister_zf), .in1(setRegister_nf), .in2(nor_1_out), .in3(1'b0), .out(multiplexer_3_out),
    .sel(ucontrol_1_seljump));
  BRegs bregs_1 (
    .R_W(and_2_out), .NReg1_Dest(ram_1_data[11:10]), .DataIn(multiplexer_2_out), .Reg1Out(bregs_1_reg1out),
    .NReg2(ram_1_data[9:8]), .Reg2Out(bregs_1_reg2out), .RegAOut(bregs_1_regaout), .RegBOut(bregs_1_regbout),
    .RegCOut(bregs_1_regcout), .RegDOut(bregs_1_regdout), .CLK(CLK_out));  // open: CLR
  Multiplexer #(.width(16), .enable("false")) multiplexer_4 (
    .in0(bregs_1_reg2out), .in1(bit_extender_1_out), .out(multiplexer_4_out), .sel(ucontrol_1_immpresent));
  LED ZF (.in(setRegister_zf));
  ALU setRegister (
    .Op1(bregs_1_reg1out), .Op2(multiplexer_4_out), .clkIn(CLK_out), .WB(ucontrol_1_wb),
    .setRegister(setRegister_setregister), .opSelector(ram_1_data[15:12]), .setFlag(and_3_out),
    .ZF(setRegister_zf), .NF(setRegister_nf), .OutputALU(setRegister_outputalu));
  LED NG (.in(setRegister_nf));
  nor nor_1 (nor_1_out, setRegister_zf, setRegister_nf);
  or or_1 (or_1_out, ucontrol_1_mem___1_alu___0, setRegister_setregister);
  not not_1 (not_1_out, ucontrol_1_l___0___s___1);
  and and_3 (and_3_out, and_2_out, ucontrol_1_setflag);
  not not_2 (not_2_out, CLK_out);
  Multiplexer #(.width(16), .enable("false")) multiplexer_5 (
    .in0(bregs_1_reg1out), .in1(bregs_1_reg2out), .out(multiplexer_5_out), .sel(not_1_out));
  RAM #(.addrWidth(16), .dataWidth(16), .bus("separate")) ram_2 (
    .addr(multiplexer_5_out), .din(bregs_1_reg2out), .data(ram_2_data), .str(ucontrol_1_l___0___s___1),
    .clk(not_2_out), .ld(1'b1));  // open: sel, clr

  // Notes on the sheet:
  //   powerOn
  //   opcode
  //   9-mov
  //   AX-0
  //   BX-4
  //   5-sub
  //   CX-8
  //   6-mul
  //   DX-12
  //   f-halt
  //   e-jump to
  //   new PC or Branch address
  //   Instruction memory
  //   jumpInstruction
  //   Reg
  //   Imm
  //   address
  //   imm value eg 10-(0a)
  //   immediatePresent
  //   R/W
  //   aluOut
  //   memOut
  //   mem/alu instruction
  //   PF
  //   WriteBack
  //   setFlags
  //   setFlag
  //   clock
  //   Reg1
  //   Reg2
  //   load/store instruction
  //   Data memory
endmodule

module BRegs (
  input  R_W,
  input  [1:0] NReg1_Dest,
  input  [1:0] NReg2,
  input  [15:0] DataIn,
  input  CLR,
  input  CLK,
  output [15:0] RegAOut,
  output [15:0] RegBOut,
  output [15:0] RegCOut,
  output [15:0] RegDOut,
  output [15:0] Reg1Out,
  output [15:0] Reg2Out
);

  wire and_1_out, and_2_out, and_3_out, and_4_out, demultiplexer_1_out0, demultiplexer_1_out1,
       demultiplexer_1_out2, demultiplexer_1_out3;
  wire [15:0] register_1_q;

  Register #(.width(16), .trigger("falling")) register_1 (.D(DataIn), .Q(register_1_q), .clk(CLK));  // open: en, clr
  Demultiplexer #(.select(2), .enable("false")) demultiplexer_1 (
    .out0(demultiplexer_1_out0), .out1(demultiplexer_1_out1), .out2(demultiplexer_1_out2),
    .out3(demultiplexer_1_out3), .in(1'b1), .sel(NReg1_Dest));
  and and_1 (and_1_out, demultiplexer_1_out0, R_W);
  and and_2 (and_2_out, demultiplexer_1_out1, R_W);
  and and_3 (and_3_out, demultiplexer_1_out2, R_W);
  and and_4 (and_4_out, demultiplexer_1_out3, R_W);
  Register #(.width(16), .trigger("high")) RegAX (
    .D(register_1_q), .Q(RegAOut), .clk(and_1_out), .clr(CLR));  // open: en
  Register #(.width(16), .trigger("high")) RegBX (
    .D(register_1_q), .Q(RegBOut), .clk(and_2_out), .clr(CLR));  // open: en
  Register #(.width(16), .trigger("high")) RegCX (
    .D(register_1_q), .Q(RegCOut), .clk(and_3_out), .clr(CLR));  // open: en
  Register #(.width(16), .trigger("high")) RegDX (
    .D(register_1_q), .Q(RegDOut), .clk(and_4_out), .clr(CLR));  // open: en
  Multiplexer #(.select(2), .width(16), .enable("false")) multiplexer_1 (
    .in0(RegAOut), .in1(RegBOut), .in2(RegCOut), .in3(RegDOut), .out(Reg1Out), .sel(NReg1_Dest));
  Multiplexer #(.select(2), .width(16), .enable("false")) multiplexer_2 (
    .in0(RegAOut), .in1(RegBOut), .in2(RegCOut), .in3(RegDOut), .out(Reg2Out), .sel(NReg2));

  // Notes on the sheet:
  //   <--- just for Debug
endmodule

module UControl (
  input  [15:0] Instruction,
  output immPresent,
  output setFlag,
  output WB,
  output Jump,
  output [1:0] selJump,
  output Mem___1_ALU___0,
  output L___0___S___1,
  output PowerOn
);

  wire and_3_out, and_4_out, nand_1_out, nand_4_out, not_2_out, not_3_out;

  not not_1 (setFlag, Instruction[15]);
  nand nand_1 (nand_1_out, ~Instruction[13], Instruction[14], Instruction[15]);  // NAND_Gate
  and and_1 (Mem___1_ALU___0, ~Instruction[12], Instruction[13], ~Instruction[14], Instruction[15]);  // AND_Gate
  and and_2 (L___0___S___1, Instruction[12], Instruction[13], ~Instruction[14], Instruction[15]);  // AND_Gate
  nand nand_2 (PowerOn, Instruction[12], Instruction[13], Instruction[14], Instruction[15]);
  nand nand_3 (immPresent, Instruction[0], Instruction[1], Instruction[2], Instruction[3], Instruction[4], Instruction[5], Instruction[6], Instruction[7]);
  and and_3 (and_3_out, nand_1_out, ~L___0___S___1);  // AND_Gate
  nand nand_4 (nand_4_out, ~Instruction[12], Instruction[13], Instruction[14], Instruction[15]);  // NAND_Gate
  and and_4 (and_4_out, and_3_out, nand_4_out);
  not not_2 (not_2_out, nand_1_out);
  not not_3 (not_3_out, nand_4_out);
  and and_5 (WB, and_4_out, PowerOn);
  or or_1 (Jump, not_2_out, not_3_out);

  assign selJump = Instruction[13:12];

  // Notes on the sheet:
  //   <--Store, JUMPZ, JUMPN, JUMPP and HALT don't have WB
endmodule

module ALU (
  input  [15:0] Op1,
  input  [15:0] Op2,
  input  [3:0] opSelector,
  input  clkIn,
  input  WB,
  input  setFlag,
  output [15:0] OutputALU,
  output setRegister,
  output ZF,
  output NF
);

  wire nor_1_out, not_1_out;
  wire [15:0] adder_1_out, and_1_out, divider_1_out, multiplier_1_out, not_2_out, or_1_out, or_2_out,
       subtractor_1_out, xor_1_out;

  not not_1 (not_1_out, clkIn);
  assign or_1_out = Op1 | Op2;  // OR_Gate or_1, 16 bits wide
  assign not_2_out = ~Op1;  // NOT_Gate not_2, 16 bits wide
  assign and_1_out = Op1 & Op2;  // AND_Gate and_1, 16 bits wide
  assign xor_1_out = Op1 ^ Op2;  // XOR_Gate xor_1, 16 bits wide
  Adder #(.width(16)) adder_1 (.a(Op1), .b(Op2), .out(adder_1_out));  // open: cin, cout
  Subtractor #(.width(16)) subtractor_1 (.a(Op1), .b(Op2), .out(subtractor_1_out));  // open: bin, bout
  Multiplier #(.width(16)) multiplier_1 (.a(Op1), .b(Op2), .out(multiplier_1_out));  // open: cin, cout
  Divider #(.width(16)) divider_1 (.a(Op1), .b(Op2), .out(divider_1_out));  // open: upper, rem
  assign or_2_out = {16{1'b0}} | Op2;  // OR_Gate or_2, 16 bits wide
  and and_2 (setRegister, not_1_out, WB);
  Multiplexer #(.select(4), .width(16), .enable("false")) multiplexer_1 (
    .in0(or_1_out), .in1(not_2_out), .in2(and_1_out), .in3(xor_1_out), .in4(adder_1_out),
    .in5(subtractor_1_out), .in6(multiplier_1_out), .in7(divider_1_out), .in8(or_2_out), .in9(or_2_out),
    .in10({16{1'b0}}), .in11({16{1'b0}}), .in12({16{1'b0}}), .in13({16{1'b0}}), .in14({16{1'b0}}),
    .in15({16{1'b0}}), .out(OutputALU), .sel(opSelector));
  nor nor_1 (nor_1_out, OutputALU[15], OutputALU[14], OutputALU[13], OutputALU[12], OutputALU[11], OutputALU[10], OutputALU[9], OutputALU[8], OutputALU[7], OutputALU[6], OutputALU[5], OutputALU[4], OutputALU[3], OutputALU[2], OutputALU[1], OutputALU[0]);
  Register #(.width(1)) u_ZF (.D(nor_1_out), .Q(ZF), .clk(setFlag));  // open: en, clr
  Register #(.width(1)) u_NF (.D(OutputALU[15]), .Q(NF), .clk(setFlag));  // open: en, clr

  // Notes on the sheet:
  //   ^--- write signal in registers bank
  //   in the falling edge.
  //   8 - 9: MOV
endmodule
